// Logisim project 19BCE237_19BCE238_19BCE245_CacheMemory copy.circ as structural Verilog: 7 circuits, main circuit main
module main (
  input  [7:0] Cache_Address,
  input  [7:0] Input,
  input  Write_Enable,
  output [7:0] Output
);

  wire Cache_Hit, CLK, not_1_out, valid_1_valid_0, valid_1_valid_1, valid_1_valid_2, valid_1_valid_3,
       Write_0, Write_1, Write_2, Write_3, Write_Through;
  wire [4:0] tag_1_tag_0, tag_1_tag_0_2, tag_1_tag_0_3, tag_1_tag_0_4;
  wire [15:0] data_register_1_data_0, data_register_1_data_1, data_register_1_data_2, data_register_1_data_3,
       ram_1_data, Selected_Block_Data, Write_Data;

  Clock u_CLK (.out(CLK));
  Cache_Line_Selector cache_line_selector_1 (
    .Line_no(Cache_Address[2:1]), .Cache_Hit(Cache_Hit), .Write_Through(Write_Through), .Write_0(Write_0),
    .Write_1(Write_1), .Write_2(Write_2), .Write_3(Write_3));
  Multiplexer #(.width(16)) multiplexer_1 (
    .in0({Selected_Block_Data[15:8], Input}), .in1({Input, Selected_Block_Data[7:0]}), .out(Write_Data),
    .sel(Cache_Address[0]), .en(Write_Through));
  and and_1 (Write_Through, Write_Enable, Cache_Hit);
  RAM #(.addrWidth(7), .dataWidth(16), .bus("separate")) ram_1 (
    .addr(Cache_Address[7:1]), .din(Write_Data), .data(ram_1_data), .str(Write_Through), .clk(CLK),
    .ld(not_1_out));  // open: sel, clr
  not not_1 (not_1_out, Cache_Hit);
  Valid valid_1 (
    .Write_0(Write_0), .Write_1(Write_1), .Write_2(Write_2), .Write_3(Write_3), .CLK(CLK),
    .Valid_0(valid_1_valid_0), .Valid_1(valid_1_valid_1), .Valid_2(valid_1_valid_2), .Valid_3(valid_1_valid_3));
  Tag tag_1 (
    .Write_0(Write_0), .Write_1(Write_1), .Write_2(Write_2), .Write_3(Write_3), .Tag(Cache_Address[7:3]),
    .CLK(CLK), .Tag_0(tag_1_tag_0), .Tag_0_2(tag_1_tag_0_2), .Tag_0_3(tag_1_tag_0_3), .Tag_0_4(tag_1_tag_0_4));
  Cache_Hit cache_hit_1 (
    .Valid_0(valid_1_valid_0), .Valid_1(valid_1_valid_1), .Valid_2(valid_1_valid_2),
    .Valid_3(valid_1_valid_3), .Line_no(Cache_Address[2:1]), .Tag_0(tag_1_tag_0), .Tag_1(tag_1_tag_0_2),
    .Tag_2(tag_1_tag_0_3), .Tag_3(tag_1_tag_0_4), .Tag(Cache_Address[7:3]), .Cache_Hit(Cache_Hit));
  Data_Register data_register_1 (
    .Write_Through(Write_Through), .Write_0(Write_0), .Write_1(Write_1), .Write_2(Write_2),
    .Write_3(Write_3), .Data_from_RAM(ram_1_data), .Write_Data(Write_Data), .CLK(CLK),
    .Data_0(data_register_1_data_0), .Data_1(data_register_1_data_1), .Data_2(data_register_1_data_2),
    .Data_3(data_register_1_data_3));
  Data_Output data_output_1 (
    .Data_0(data_register_1_data_0), .Data_0_2(data_register_1_data_1), .Data_0_3(data_register_1_data_2),
    .Data_0_4(data_register_1_data_3), .Line_no(Cache_Address[2:1]), .Cache_Hit(Cache_Hit),
    .Word_Select(Cache_Address[0]), .Selected_Block_Data(Selected_Block_Data), .Output(Output));

  // Other names for the same wires on the sheet: Word_Select = Cache_Address[0]; Line_no[1:0] = Cache_Address[2:1];
  //   Tag[4:0] = Cache_Address[7:3]

  // Notes on the sheet:
  //   Cache Line Selector
  //   RAM size
  //   128 x 16 bits = 2 kB
  //   Main Memory
  //   DIRECT MAPPED CACHE MEMORY
  //   Data from RAM
  //   Cache size
  //   4 x 16 bits = 64 bits
  //   Prepared by : 
  //   19BCE237 - SAKSHI SANGHAVI
  //   19BCE238 - HARSHIL SANGHVI
  //   19BCE245 - AAYUSH SHAH
endmodule

module Valid (
  input  Write_0,
  input  Write_1,
  input  Write_2,
  input  Write_3,
  input  CLK,
  output Valid_0,
  output Valid_1,
  output Valid_2,
  output Valid_3
);

  Register #(.width(1)) u_Valid_0 (.D(1'b1), .en(Write_0), .Q(Valid_0), .clk(CLK));  // open: clr
  Register #(.width(1)) u_Valid_1 (.D(1'b1), .en(Write_1), .Q(Valid_1), .clk(CLK));  // open: clr
  Register #(.width(1)) u_Valid_2 (.D(1'b1), .en(Write_2), .Q(Valid_2), .clk(CLK));  // open: clr
  Register #(.width(1)) u_Valid_3 (.D(1'b1), .en(Write_3), .Q(Valid_3), .clk(CLK));  // open: clr
endmodule

module Tag (
  input  [4:0] Tag,
  input  Write_0,
  input  Write_1,
  input  Write_2,
  input  Write_3,
  input  CLK,
  output [4:0] Tag_0,
  output [4:0] Tag_0_2,
  output [4:0] Tag_0_3,
  output [4:0] Tag_0_4
);

  Register #(.width(5)) u_Tag_0 (.D(Tag), .en(Write_0), .Q(Tag_0), .clk(CLK));  // open: clr
  Register #(.width(5)) Tag_1 (.D(Tag), .en(Write_1), .Q(Tag_0_2), .clk(CLK));  // open: clr
  Register #(.width(5)) Tag_2 (.D(Tag), .en(Write_2), .Q(Tag_0_3), .clk(CLK));  // open: clr
  Register #(.width(5)) Tag_3 (.D(Tag), .en(Write_3), .Q(Tag_0_4), .clk(CLK));  // open: clr
endmodule

// Data
module Data_Register (
  input  [15:0] Data_from_RAM,
  input  [15:0] Write_Data,
  input  Write_Through,
  input  Write_0,
  input  Write_1,
  input  Write_2,
  input  Write_3,
  input  CLK,
  output [15:0] Data_0,
  output [15:0] Data_1,
  output [15:0] Data_2,
  output [15:0] Data_3
);

  wire [15:0] multiplexer_1_out;

  Multiplexer #(.width(16), .enable("false")) multiplexer_1 (
    .in0(Data_from_RAM), .in1(Write_Data), .out(multiplexer_1_out), .sel(Write_Through));
  Register #(.width(16)) u_Data_0 (.D(multiplexer_1_out), .en(Write_0), .Q(Data_0), .clk(CLK));  // open: clr
  Register #(.width(16)) u_Data_1 (.D(multiplexer_1_out), .en(Write_1), .Q(Data_1), .clk(CLK));  // open: clr
  Register #(.width(16)) u_Data_2 (.D(multiplexer_1_out), .en(Write_2), .Q(Data_2), .clk(CLK));  // open: clr
  Register #(.width(16)) Dara_3 (.D(multiplexer_1_out), .en(Write_3), .Q(Data_3), .clr(CLK));  // open: clk
endmodule

module Cache_Line_Selector (
  input  [1:0] Line_no,
  input  Cache_Hit,
  input  Write_Through,
  output Write_0,
  output Write_1,
  output Write_2,
  output Write_3
);

  wire not_1_out, or_1_out;

  not not_1 (not_1_out, Cache_Hit);
  Decoder #(.select(2), .disabled(0)) decoder_1 (
    .out0(Write_0), .out1(Write_1), .out2(Write_2), .out3(Write_3), .sel(Line_no), .en(or_1_out));
  or or_1 (or_1_out, not_1_out, Write_Through);
endmodule

// Output
module Data_Output (
  input  [15:0] Data_0,
  input  [15:0] Data_0_2,
  input  [15:0] Data_0_3,
  input  [15:0] Data_0_4,
  input  [1:0] Line_no,
  input  Cache_Hit,
  input  Word_Select,
  output [15:0] Selected_Block_Data,
  output [7:0] Output
);

  Multiplexer #(.select(2), .width(16)) multiplexer_1 (
    .in0(Data_0), .in1(Data_0_2), .in2(Data_0_3), .in3(Data_0_4), .out(Selected_Block_Data), .sel(Line_no),
    .en(Cache_Hit));
  Multiplexer #(.width(8)) multiplexer_2 (
    .in0(Selected_Block_Data[7:0]), .in1(Selected_Block_Data[15:8]), .out(Output), .sel(Word_Select),
    .en(Cache_Hit));
endmodule

// Cache Hit
module Cache_Hit (
  input  Valid_0,
  input  Valid_1,
  input  Valid_2,
  input  Valid_3,
  input  [1:0] Line_no,
  input  [4:0] Tag_0,
  input  [4:0] Tag,
  input  [4:0] Tag_1,
  input  [4:0] Tag_2,
  input  [4:0] Tag_3,
  output Cache_Hit
);

  wire comparator_1_eq, multiplexer_1_out;
  wire [4:0] multiplexer_2_out;

  Multiplexer #(.select(2), .enable("false")) multiplexer_1 (
    .in0(Valid_0), .in1(Valid_1), .in2(Valid_2), .in3(Valid_3), .out(multiplexer_1_out), .sel(Line_no));
  Multiplexer #(.select(2), .width(5), .enable("false")) multiplexer_2 (
    .in0(Tag_0), .in1(Tag_1), .in2(Tag_2), .in3(Tag_3), .out(multiplexer_2_out), .sel(Line_no));
  Comparator #(.width(5), .mode("unsigned")) comparator_1 (
    .a(Tag), .b(multiplexer_2_out), .eq(comparator_1_eq));  // open: gt, lt
  and and_1 (Cache_Hit, multiplexer_1_out, comparator_1_eq);
endmodule
