// Logisim project 9B Cache Memory.circ as structural Verilog: 1 circuit, main circuit Cache Memory
module Cache_Memory (
  input  [7:0] Cache_Address,
  input  [7:0] Input_Data,
  input  Write_Enable,
  output [7:0] Data_Output
);

  wire Cache_Hit, Clock_out, decoder_1_out0, decoder_1_out1, decoder_1_out2, decoder_1_out3, decoder_2_out0,
       decoder_2_out1, decoder_2_out2, decoder_2_out3, multiplexer_5_out, not_1_out, not_2_out, valid0,
       valid1, valid2, valid3, Write_0, Write_1, Write_2, Write_3, Write_Through, xnor_1_out, xnor_2_out,
       xnor_3_out, xnor_4_out, xnor_5_out;
  wire [4:0] multiplexer_4_out, Tag_0, Tag_1, Tag_2, Tag_3;
  wire [15:0] Data_0, Data_1, Data_2, Data_3, multiplexer_2_out, New_Data_from_RAM, Selected_Block_Data,
       WriteT_Data;

  Clock Clock (.out(Clock_out));
  Multiplexer #(.width(16)) multiplexer_1 (
    .in0({Selected_Block_Data[15:8], Input_Data}), .in1({Input_Data, Selected_Block_Data[7:0]}),
    .out(WriteT_Data), .sel(Cache_Address[0]), .en(Write_Through));
  and and_1 (Write_Through, Write_Enable, Cache_Hit);
  not not_1 (not_1_out, Cache_Hit);
  Decoder #(.select(2), .disabled(0)) decoder_1 (
    .out0(decoder_1_out0), .out1(decoder_1_out1), .out2(decoder_1_out2), .out3(decoder_1_out3),
    .sel(Cache_Address[2:1]), .en(not_2_out));
  not not_2 (not_2_out, Cache_Hit);
  Decoder #(.select(2), .disabled(0)) decoder_2 (
    .out0(decoder_2_out0), .out1(decoder_2_out1), .out2(decoder_2_out2), .out3(decoder_2_out3),
    .sel(Cache_Address[2:1]), .en(Write_Through));
  RAM #(.addrWidth(7), .dataWidth(16), .bus("separate")) ram_1 (
    .addr(Cache_Address[7:1]), .din(WriteT_Data), .data(New_Data_from_RAM), .str(Write_Through),
    .clk(Clock_out), .ld(not_1_out));  // open: sel, clr
  or or_1 (Write_0, decoder_1_out0, decoder_2_out0);
  or or_2 (Write_1, decoder_1_out1, decoder_2_out1);
  or or_3 (Write_2, decoder_1_out2, decoder_2_out2);
  or or_4 (Write_3, decoder_1_out3, decoder_2_out3);
  Register #(.width(1)) isValid_3 (.D(1'b1), .en(Write_3), .Q(valid3), .clk(Clock_out));  // open: clr
  Register #(.width(1)) isValid_1 (.D(1'b1), .en(Write_1), .Q(valid1), .clk(Clock_out));  // open: clr
  Register #(.width(1)) isValid_2 (.D(1'b1), .en(Write_2), .Q(valid2), .clk(Clock_out));  // open: clr
  Register #(.width(1)) isValid_0 (.D(1'b1), .en(Write_0), .Q(valid0), .clk(Clock_out));  // open: clr
  Register #(.width(5)) u_Tag_3 (.D(Cache_Address[7:3]), .en(Write_3), .Q(Tag_3), .clk(Clock_out));  // open: clr
  Register #(.width(5)) u_Tag_1 (.D(Cache_Address[7:3]), .en(Write_1), .Q(Tag_1), .clk(Clock_out));  // open: clr
  Register #(.width(5)) u_Tag_2 (.D(Cache_Address[7:3]), .en(Write_2), .Q(Tag_2), .clk(Clock_out));  // open: clr
  Register #(.width(5)) u_Tag_0 (.D(Cache_Address[7:3]), .en(Write_0), .Q(Tag_0), .clk(Clock_out));  // open: clr
  Register #(.width(16)) Block_3 (.D(multiplexer_2_out), .en(Write_3), .Q(Data_3), .clk(Clock_out));  // open: clr
  Multiplexer #(.width(16), .enable("false")) multiplexer_2 (
    .in0(New_Data_from_RAM), .in1(WriteT_Data), .out(multiplexer_2_out), .sel(Write_Through));
  Register #(.width(16)) Block_1 (.D(multiplexer_2_out), .en(Write_1), .Q(Data_1), .clk(Clock_out));  // open: clr
  Register #(.width(16)) Block_2 (.D(multiplexer_2_out), .en(Write_2), .Q(Data_2), .clk(Clock_out));  // open: clr
  Register #(.width(16)) Block_0 (.D(multiplexer_2_out), .en(Write_0), .Q(Data_0), .clk(Clock_out));  // open: clr
  Multiplexer #(.select(2), .width(16)) multiplexer_3 (
    .in0(Data_0), .in1(Data_1), .in2(Data_2), .in3(Data_3), .out(Selected_Block_Data),
    .sel(Cache_Address[2:1]), .en(Cache_Hit));
  Multiplexer #(.select(2), .width(5), .enable("false")) multiplexer_4 (
    .in0(Tag_0), .in1(Tag_1), .in2(Tag_2), .in3(Tag_3), .out(multiplexer_4_out), .sel(Cache_Address[2:1]));
  Multiplexer #(.select(2), .enable("false")) multiplexer_5 (
    .in0(valid0), .in1(valid1), .in2(valid2), .in3(valid3), .out(multiplexer_5_out), .sel(Cache_Address[2:1]));
  Multiplexer #(.width(8)) multiplexer_6 (
    .in0(Selected_Block_Data[7:0]), .in1(Selected_Block_Data[15:8]), .out(Data_Output),
    .sel(Cache_Address[0]), .en(Cache_Hit));
  xnor xnor_1 (xnor_1_out, multiplexer_4_out[0], Cache_Address[3]);
  xnor xnor_2 (xnor_2_out, multiplexer_4_out[1], Cache_Address[4]);
  xnor xnor_3 (xnor_3_out, multiplexer_4_out[2], Cache_Address[5]);
  xnor xnor_4 (xnor_4_out, multiplexer_4_out[3], Cache_Address[6]);
  xnor xnor_5 (xnor_5_out, multiplexer_4_out[4], Cache_Address[7]);
  and and_2 (Cache_Hit, xnor_1_out, xnor_2_out, xnor_3_out, xnor_4_out, xnor_5_out, multiplexer_5_out);

  // Other names for the same wires on the sheet: Word_Select = Cache_Address[0];
  //   Block_Select[1:0] = Cache_Address[2:1]; Tag_IN[4:0] = Cache_Address[7:3]

  // Notes on the sheet:
  //   No of Blocks = 4
  //   No of Words per block = 2
  //   Assuming One Word in Main holds one block of two actual words
  //   Main Memory
  //   Size of Word = 8bits
  //   I have made this myself (16BCE059) by the following the instructions given on this site
  //   https://www.cs.grinnell.edu/~davisjan/csc/211/2013F/labs/lab9.direct-mapped-cache.shtml
  //   Therefore, Tag is 5 bits
  //   Index is 3 bits, 2 bits to select the block and 1 bit to select the word
endmodule
