// Logisim project Innovative_Assignment.circ as structural Verilog: 1 circuit, main circuit main
module main (
  input  [7:0] Cache_Address,
  input  [7:0] Input,
  input  Write_Enable,
  output [7:0] Output
);

  wire Cache_Hit, CLK, main_2_p6, main_2_p7, main_2_p8, main_2_p9, main_3_p7, main_3_p8, main_3_p9,
       main_3_p10, main_5_p9, main_5_p10, main_5_p11, main_5_p12, not_1_out, Write_0, Write_1, Write_2,
       Write_3, Write_Through;
  wire [15:0] ram_1_data, Selected_Block_Data, Write_Data;

  Clock u_CLK (.out(CLK));
  // Cache_Line_Selector_main main_1: pin names not known; wires that end beside it: Cache_Address[2:1], Cache_Hit, Write_Through, Write_0, Write_1, Write_2, Write_3
  Multiplexer #(.width(16)) multiplexer_1 (
    .in0({Selected_Block_Data[15:8], Input}), .in1({Input, Selected_Block_Data[7:0]}), .out(Write_Data),
    .sel(Cache_Address[0]), .en(Write_Through));
  and and_1 (Write_Through, Write_Enable, Cache_Hit);
  RAM #(.addrWidth(7), .dataWidth(16), .bus("separate")) ram_1 (
    .addr(Cache_Address[7:1]), .din(Write_Data), .data(ram_1_data), .str(Write_Through), .clk(CLK),
    .ld(not_1_out));  // open: sel, clr
  not not_1 (not_1_out, Cache_Hit);
  // Valid_main main_2: pin names not known; wires that end beside it: Write_0, Write_1, Write_2, Write_3, CLK, main_2_p6, main_2_p7, main_2_p8, main_2_p9
  // Tag_main main_3: pin names not known; wires that end beside it: Write_0, Write_1, Write_2, Write_3, Cache_Address[7:3], CLK, main_3_p7, main_3_p8, main_3_p9, main_3_p10
  // Cache_Hit_main main_4: pin names not known; wires that end beside it: main_2_p6, main_2_p7, main_2_p8, main_2_p9, Cache_Address[2:1], main_3_p7, main_3_p8, main_3_p9, main_3_p10, Cache_Address[7:3], Cache_Hit
  // Write_Data_Register_main main_5: pin names not known; wires that end beside it: Write_Through, Write_0, Write_1, Write_2, Write_3, ram_1_data, CLK, Write_Data, main_5_p9, main_5_p10, main_5_p11, main_5_p12
  // Data_Output_main main_6: pin names not known; wires that end beside it: main_5_p9, main_5_p10, main_5_p11, main_5_p12, Cache_Address[2:1], Cache_Hit, Cache_Address[0], Selected_Block_Data, Output

  // Other names for the same wires on the sheet: Word_Select = Cache_Address[0]; Line_no[1:0] = Cache_Address[2:1];
  //   Tag[4:0] = Cache_Address[7:3]

  // Notes on the sheet:
  //   Cache Line Selector
  //   Main Memory
endmodule
